# Fritzing sketch wiring_diagram_g211 (saved by Fritzing 0.9.2b)
breadboards: 2

parts:
  Part1 = Arduino Uno (Rev3)
  Part2 = PowerBoost 1000 Basic
  Part3 = XBee Explorer Regulated
  LED1 = smd LED [color="Red (633nm)" package="1206 [SMD]"]
  R1 = Resistor [tolerance=±5% resistance=330 package="2010 [SMD]"]
  U1 = 2.5mm Audio Jack [package=stereojack2.5mm_smd]
  Part4 = XBee Explorer Regulated
  R2 = Resistor [tolerance=±5% resistance=330 package="2010 [SMD]"]
  LED2 = smd LED [color="Red (633nm)" package="1206 [SMD]"]
  U3 = POT [package=trim_pot]
  Part5 = PowerBoost 1000 Basic

nets:
  N1: Part1.D10_PWM/SS, LED1.anode
  N2: Part1.D0/RX, Part3.DOUT
  GND: Part1.GND, Part2.GND, Part3.GND, R1.Pin_0, U1.SLEEVE
  VIN: Part1.VIN, Part2.5.0V, Part3.5V, U1.LEFT
  N3: LED1.cathode, R1.Pin_1
  GND_2: Part4.GND, R2.Pin_0, Part5.GND
  N4: Part4.3.3V, LED2.anode, U3.A
  N5: Part4.DIO4, R2.Pin_1, LED2.cathode, U3.S
  N6: Part4.5V, Part5.5.0V

notes:
  Controller
  (see repo for config)
  Remote
  (see repo for config)
  ^ debug LED
  USB A, 5V wart-> mini audio jack for power
  Pot is hacked to be a switch. when 'clicked' into place, it closes the switch. all other positions opens the switch.

custom parts:
  PowerBoost 1000 Basic: The PowerBoost 1000 is a little DC/DC boost converter module that can run from 1.8V batteries or higher, and convert the battery output to 5.2V DC for running your 5V projects. At its heart is a TPS61030 boost converter from TI. This boost converter chip has some really nice extras such as low battery detection, 4A internal switch, synchronous conversion, excellent efficiency, and 700KHz high-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
